// Logisim project chapter-1.circ as structural Verilog: 15 circuits, main circuit 3输入多数表决器
// 发
module \_3输入多数表决器  (
  input  a,
  input  b,
  input  c,
  output \输出 
);

  wire and_1_out, and_2_out, and_3_out;

  and and_1 (and_1_out, a, b);
  and and_2 (and_2_out, a, c);
  and and_3 (and_3_out, b, c);
  or or_1 (\输出 , and_1_out, and_2_out, and_3_out);

  // Notes on the sheet:
  //   3输入多数表决器
endmodule

module \CMOS构造或门  (
  input  x,
  input  y,
  output out
);

  wire transistor_1_out, transistor_2_out;

  Transistor transistor_1 (.in(1'b1), .out(transistor_1_out), .gate(x));
  Transistor transistor_2 (.in(transistor_1_out), .out(transistor_2_out), .gate(y));
  Transistor #(.\type ("n")) transistor_3 (.in(1'b0), .out(transistor_2_out), .gate(x));
  Transistor #(.\type ("n")) transistor_4 (.in(1'b0), .out(transistor_2_out), .gate(y));
  Transistor transistor_5 (.in(1'b1), .out(out), .gate(transistor_2_out));
  Transistor #(.\type ("n")) transistor_6 (.in(1'b0), .out(out), .gate(transistor_2_out));

  // Notes on the sheet:
  //   VDD
  //   GND
  //   CMOS构造或门
endmodule

module \_4位奇偶校验电路_自动生成  (
  input  N0,
  input  N1,
  input  N2,
  input  N3,
  output EVEN,
  output ODD
);

  wire and_1_out, and_2_out, and_3_out, and_4_out, and_5_out, and_6_out, and_7_out, and_8_out, and_9_out,
       and_10_out, and_11_out, and_12_out, and_13_out, and_14_out, and_15_out, and_16_out, not_1_out,
       not_2_out, not_3_out, not_4_out, not_5_out, not_6_out, not_7_out, not_8_out, not_9_out, not_10_out,
       not_11_out, not_12_out, not_13_out, not_14_out, not_15_out, not_16_out, not_17_out, not_18_out,
       not_19_out, not_20_out, not_21_out, not_22_out, not_23_out, not_24_out, not_25_out, not_26_out,
       not_27_out, not_28_out, not_29_out, not_30_out, not_31_out, not_32_out;

  not not_1 (not_1_out, N0);
  not not_2 (not_2_out, N1);
  not not_3 (not_3_out, N2);
  not not_4 (not_4_out, N3);
  not not_5 (not_5_out, N0);
  not not_6 (not_6_out, N1);
  not not_7 (not_7_out, N0);
  not not_8 (not_8_out, N2);
  not not_9 (not_9_out, N0);
  not not_10 (not_10_out, N3);
  not not_11 (not_11_out, N1);
  not not_12 (not_12_out, N2);
  not not_13 (not_13_out, N1);
  not not_14 (not_14_out, N3);
  not not_15 (not_15_out, N2);
  not not_16 (not_16_out, N3);
  not not_17 (not_17_out, N0);
  not not_18 (not_18_out, N1);
  not not_19 (not_19_out, N2);
  not not_20 (not_20_out, N0);
  not not_21 (not_21_out, N1);
  not not_22 (not_22_out, N3);
  not not_23 (not_23_out, N0);
  not not_24 (not_24_out, N2);
  not not_25 (not_25_out, N3);
  not not_26 (not_26_out, N0);
  not not_27 (not_27_out, N1);
  not not_28 (not_28_out, N2);
  not not_29 (not_29_out, N3);
  not not_30 (not_30_out, N1);
  not not_31 (not_31_out, N2);
  not not_32 (not_32_out, N3);
  and and_1 (and_1_out, not_1_out, not_2_out, not_3_out, not_4_out);
  and and_2 (and_2_out, not_5_out, not_6_out, N2, N3);
  and and_3 (and_3_out, not_7_out, N1, not_8_out, N3);
  and and_4 (and_4_out, not_9_out, N1, N2, not_10_out);
  and and_5 (and_5_out, N0, not_11_out, not_12_out, N3);
  and and_6 (and_6_out, N0, not_13_out, N2, not_14_out);
  and and_7 (and_7_out, N0, N1, not_15_out, not_16_out);
  and and_8 (and_8_out, N0, N1, N2, N3);
  and and_9 (and_9_out, not_17_out, not_18_out, not_19_out, N3);
  and and_10 (and_10_out, not_20_out, not_21_out, N2, not_22_out);
  and and_11 (and_11_out, not_23_out, N1, not_24_out, not_25_out);
  and and_12 (and_12_out, not_26_out, N1, N2, N3);
  and and_13 (and_13_out, N0, not_27_out, not_28_out, not_29_out);
  and and_14 (and_14_out, N0, not_30_out, N2, N3);
  and and_15 (and_15_out, N0, N1, not_31_out, N3);
  and and_16 (and_16_out, N0, N1, N2, not_32_out);
  or or_1 (EVEN, and_1_out, and_2_out, and_3_out, and_4_out, and_5_out, and_6_out, and_7_out, and_8_out);
  or or_2 (ODD, and_9_out, and_10_out, and_11_out, and_12_out, and_13_out, and_14_out, and_15_out, and_16_out);
endmodule

module \_4位奇偶校验电路  (
  input  N0,
  input  N1,
  input  N2,
  input  N3,
  output EVEN,
  output ODD
);

  wire xor_1_out, xor_2_out;

  xor xor_1 (xor_1_out, N0, N1);
  xor xor_2 (xor_2_out, N2, N3);
  xor xor_3 (ODD, xor_1_out, xor_2_out);
  not not_1 (EVEN, ODD);

  // Notes on the sheet:
  //   4位奇偶校验电路
endmodule

module \LED点阵显示名字  (
);

  DotMatrix dotmatrix_1 (.col0({7{1'b1}}), .col1(7'b1001000), .col2(7'b1001000), .col3(7'b1001000), .col4(7'b1001000));
  DotMatrix dotmatrix_2 (.col0({7{1'b1}}), .col1(7'b0000011), .col2({7{1'b1}}), .col3(7'b0000011), .col4({7{1'b1}}));
  DotMatrix dotmatrix_3 (.col0({7{1'b1}}), .col1(7'b1100000), .col2({7{1'b1}}), .col3(7'b1100000), .col4({7{1'b1}}));

  // Notes on the sheet:
  //   F
  //   W
  //   LED点阵显示名字
  //   M
endmodule

module \_3_8译码器  (
  input  E3,
  input  E2,
  input  E1,
  input  I0,
  input  I1,
  input  I2,
  output O0,
  output O1,
  output O2,
  output O3,
  output O4,
  output O5,
  output O6,
  output O7
);

  wire and_1_out, not_1_out, not_2_out, not_3_out, not_4_out, not_5_out, not_6_out;

  not not_1 (not_1_out, I0);
  not not_2 (not_2_out, I1);
  not not_3 (not_3_out, I2);
  and and_1 (and_1_out, E3, ~E2, ~E1);  // AND_Gate
  not not_4 (not_4_out, not_1_out);
  not not_5 (not_5_out, not_2_out);
  not not_6 (not_6_out, not_3_out);
  nand nand_1 (O0, not_1_out, not_2_out, not_3_out, and_1_out);
  nand nand_2 (O1, not_2_out, not_3_out, not_4_out, and_1_out);
  nand nand_3 (O2, not_1_out, not_3_out, not_5_out, and_1_out);
  nand nand_4 (O3, not_3_out, not_4_out, not_5_out, and_1_out);
  nand nand_5 (O4, not_1_out, not_2_out, not_6_out, and_1_out);
  nand nand_6 (O5, not_2_out, not_4_out, not_6_out, and_1_out);
  nand nand_7 (O6, not_1_out, not_5_out, not_6_out, and_1_out);
  nand nand_8 (O7, and_1_out, not_5_out, not_6_out, not_4_out);

  // Notes on the sheet:
  //   3-8译码器
endmodule

module \优先级编码器  (
  input  O0,
  input  O1,
  input  O2,
  input  O3,
  input  O4,
  input  O5,
  input  O6,
  input  O7
);

  wire [2:0] priority_encoder_1_out;

  Priority_Encoder priority_encoder_1 (
    .in0(O0), .in1(O1), .in2(O2), .in3(O3), .in4(O4), .in5(O5), .in6(O6), .in7(O7),
    .out(priority_encoder_1_out));  // open: gs, en_out, en_in
  // Probe on priority_encoder_1_out[0]
  // Probe on priority_encoder_1_out[1]
  // Probe on priority_encoder_1_out[2]
  Hex_Digit_Display hex_digit_display_1 (.value({1'b0, priority_encoder_1_out}));  // open: dp

  // Notes on the sheet:
  //   优先级编码器测试电路
  //   优先级：O7>O6>O5>O4>O3>O2>O1>O0
endmodule

module \_2选1多路选择器  (
  input  Ai,
  input  Bi,
  input  S,
  output out_4
);

  wire and_1_out, and_2_out;

  and and_1 (and_1_out, Ai, ~S);  // AND_Gate
  and and_2 (and_2_out, S, Bi);
  or or_1 (out_4, and_1_out, and_2_out);

  // Notes on the sheet:
  //   2选1多路选择器
endmodule

module \_4选1多路选择器  (
  input  A,
  input  B,
  input  C,
  input  D,
  input  S0,
  input  S1,
  output F
);

  wire \n2选1多路选择器_1_out_4 , \n2选1多路选择器_2_out_4 ;

  \_2选1多路选择器  \u_2选1多路选择器_1  (.Ai(A), .Bi(B), .out_4(\n2选1多路选择器_1_out_4 ), .S(S0));
  \_2选1多路选择器  \u_2选1多路选择器_2  (.Ai(C), .Bi(D), .out_4(\n2选1多路选择器_2_out_4 ), .S(S0));
  \_2选1多路选择器  \u_2选1多路选择器_3  (.Ai(\n2选1多路选择器_1_out_4 ), .Bi(\n2选1多路选择器_2_out_4 ), .out_4(F), .S(S1));

  // Notes on the sheet:
  //   4选1多路选择器
endmodule

module \X_全加器_FA_课本实现  (
  input  A,
  input  B,
  input  Cin,
  output Count,
  output F
);

  wire and_1_out, and_2_out, and_3_out;

  and and_1 (and_1_out, A, B);
  and and_2 (and_2_out, B, Cin);
  and and_3 (and_3_out, A, Cin);
  or or_1 (Count, and_1_out, and_2_out, and_3_out);
  xor xor_1 (F, A, B, Cin);

  // Notes on the sheet:
  //   全加器（FA）课本实现
endmodule

module \全加器_FA  (
  input  A,
  input  B,
  input  Cin,
  output F,
  output count
);

  wire nand_1_out, nand_2_out, xor_1_out;

  xor xor_1 (xor_1_out, A, B);
  nand nand_1 (nand_1_out, B, A);
  xor xor_2 (F, xor_1_out, Cin);
  nand nand_2 (nand_2_out, Cin, xor_1_out);
  nand nand_3 (count, nand_2_out, nand_1_out);

  // Notes on the sheet:
  //   全加器（FA）
endmodule

module \_4位串行进位加法器  (
  input  [3:0] in_1,
  input  [3:0] in_2
);

  wire \全加器_fa_1_count , \全加器_fa_2_count , \全加器_fa_3_count ;
  wire [3:0] \全加器_fa_1_f ;

  Hex_Digit_Display hex_digit_display_1 (.value(in_1));  // open: dp
  Hex_Digit_Display hex_digit_display_2 (.value(in_2));  // open: dp
  \全加器_FA  \u_全加器_fa_1  (.A(in_1[0]), .B(in_2[0]), .Cin(1'b0), .F(\全加器_fa_1_f [0]), .count(\全加器_fa_1_count ));
  \全加器_FA  \u_全加器_fa_2  (
    .A(in_1[1]), .B(in_2[1]), .Cin(\全加器_fa_1_count ), .F(\全加器_fa_1_f [1]), .count(\全加器_fa_2_count ));
  \全加器_FA  \u_全加器_fa_3  (
    .A(in_1[2]), .B(in_2[2]), .Cin(\全加器_fa_2_count ), .F(\全加器_fa_1_f [2]), .count(\全加器_fa_3_count ));
  \全加器_FA  \u_全加器_fa_4  (.A(in_1[3]), .B(in_2[3]), .Cin(\全加器_fa_3_count ), .F(\全加器_fa_1_f [3]));  // open: count
  Hex_Digit_Display hex_digit_display_3 (.value(\全加器_fa_1_f ));  // open: dp

  // Notes on the sheet:
  //   0
  //   1
  //   4位串行进位加法器
  //   2
  //   3
endmodule

module \计数器十进制计数并输出  (
);

  wire clock_1_out, counter_2_carry;
  wire [3:0] counter_1_q, counter_2_q;

  Counter #(.width(4), .max('h9)) counter_1 (
    .count(counter_2_carry), .Q(counter_1_q), .clk(clock_1_out));  // open: load, D, carry, clr, preset, down
  Hex_Digit_Display hex_digit_display_1 (.value(counter_1_q));  // open: dp
  Clock clock_1 (.out(clock_1_out));
  Hex_Digit_Display hex_digit_display_2 (.value(counter_2_q));  // open: dp
  Counter #(.width(4), .max('h9)) counter_2 (
    .Q(counter_2_q), .carry(counter_2_carry), .clk(clock_1_out));  // open: load, D, count, clr, preset, down

  // Notes on the sheet:
  //   计数器十进制计数并输出
endmodule

module \寄存器堆Regfile实现  (
  input  [4:0] R1_num,
  input  [4:0] R2_num,
  input  [4:0] Wtite_Reg_num,
  input  Writw_Enable,
  input  Clock,
  input  [31:0] Din,
  output [31:0] Reg1Out,
  output [31:0] Reg2Out
);

  wire and_1_out, and_2_out, and_3_out, and_4_out, and_5_out, and_6_out, and_7_out, and_8_out, and_9_out,
       and_10_out, and_11_out, and_12_out, and_13_out, and_14_out, and_15_out, and_16_out, and_17_out,
       and_18_out, and_19_out, and_20_out, and_21_out, and_22_out, and_23_out, and_24_out, and_25_out,
       and_26_out, and_27_out, and_28_out, and_29_out, and_30_out, and_31_out, and_32_out, decoder_1_out0,
       decoder_1_out1, decoder_1_out2, decoder_1_out3, decoder_1_out4, decoder_1_out5, decoder_1_out6,
       decoder_1_out7, decoder_1_out8, decoder_1_out9, decoder_1_out10, decoder_1_out11, decoder_1_out12,
       decoder_1_out13, decoder_1_out14, decoder_1_out15, decoder_1_out16, decoder_1_out17, decoder_1_out18,
       decoder_1_out19, decoder_1_out20, decoder_1_out21, decoder_1_out22, decoder_1_out23, decoder_1_out24,
       decoder_1_out25, decoder_1_out26, decoder_1_out27, decoder_1_out28, decoder_1_out29, decoder_1_out30,
       decoder_1_out31;
  wire [31:0] register_1_q, register_2_q, register_3_q, register_4_q, register_5_q, register_6_q,
       register_7_q, register_8_q, register_9_q, register_10_q, register_11_q, register_12_q, register_13_q,
       register_14_q, register_15_q, register_16_q, register_17_q, register_18_q, register_19_q,
       register_20_q, register_21_q, register_22_q, register_23_q, register_24_q, register_25_q,
       register_26_q, register_27_q, register_28_q, register_29_q, register_30_q, register_31_q,
       register_32_q;

  Decoder #(.select(5), .enable("false")) decoder_1 (
    .out0(decoder_1_out0), .out1(decoder_1_out1), .out2(decoder_1_out2), .out3(decoder_1_out3),
    .out4(decoder_1_out4), .out5(decoder_1_out5), .out6(decoder_1_out6), .out7(decoder_1_out7),
    .out8(decoder_1_out8), .out9(decoder_1_out9), .out10(decoder_1_out10), .out11(decoder_1_out11),
    .out12(decoder_1_out12), .out13(decoder_1_out13), .out14(decoder_1_out14), .out15(decoder_1_out15),
    .out16(decoder_1_out16), .out17(decoder_1_out17), .out18(decoder_1_out18), .out19(decoder_1_out19),
    .out20(decoder_1_out20), .out21(decoder_1_out21), .out22(decoder_1_out22), .out23(decoder_1_out23),
    .out24(decoder_1_out24), .out25(decoder_1_out25), .out26(decoder_1_out26), .out27(decoder_1_out27),
    .out28(decoder_1_out28), .out29(decoder_1_out29), .out30(decoder_1_out30), .out31(decoder_1_out31),
    .sel(Wtite_Reg_num));
  and and_1 (and_1_out, Clock, Writw_Enable, decoder_1_out0);
  and and_2 (and_2_out, Clock, Writw_Enable, decoder_1_out1);
  and and_3 (and_3_out, Clock, Writw_Enable, decoder_1_out2);
  and and_4 (and_4_out, Clock, Writw_Enable, decoder_1_out3);
  and and_5 (and_5_out, Clock, Writw_Enable, decoder_1_out4);
  and and_6 (and_6_out, Clock, Writw_Enable, decoder_1_out5);
  and and_7 (and_7_out, Clock, Writw_Enable, decoder_1_out6);
  and and_8 (and_8_out, Clock, Writw_Enable, decoder_1_out7);
  and and_9 (and_9_out, Clock, Writw_Enable, decoder_1_out8);
  and and_10 (and_10_out, Clock, Writw_Enable, decoder_1_out9);
  and and_11 (and_11_out, Clock, Writw_Enable, decoder_1_out10);
  and and_12 (and_12_out, Clock, Writw_Enable, decoder_1_out11);
  and and_13 (and_13_out, Clock, Writw_Enable, decoder_1_out12);
  and and_14 (and_14_out, Clock, Writw_Enable, decoder_1_out13);
  and and_15 (and_15_out, Clock, Writw_Enable, decoder_1_out14);
  and and_16 (and_16_out, Clock, Writw_Enable, decoder_1_out15);
  and and_17 (and_17_out, Clock, Writw_Enable, decoder_1_out16);
  and and_18 (and_18_out, Clock, Writw_Enable, decoder_1_out17);
  and and_19 (and_19_out, Clock, Writw_Enable, decoder_1_out18);
  and and_20 (and_20_out, Clock, Writw_Enable, decoder_1_out19);
  and and_21 (and_21_out, Clock, Writw_Enable, decoder_1_out20);
  and and_22 (and_22_out, Clock, Writw_Enable, decoder_1_out21);
  and and_23 (and_23_out, Clock, Writw_Enable, decoder_1_out22);
  and and_24 (and_24_out, Clock, Writw_Enable, decoder_1_out23);
  and and_25 (and_25_out, Clock, Writw_Enable, decoder_1_out24);
  and and_26 (and_26_out, Clock, Writw_Enable, decoder_1_out25);
  and and_27 (and_27_out, Clock, Writw_Enable, decoder_1_out26);
  and and_28 (and_28_out, Clock, Writw_Enable, decoder_1_out27);
  and and_29 (and_29_out, Clock, Writw_Enable, decoder_1_out28);
  and and_30 (and_30_out, Clock, Writw_Enable, decoder_1_out29);
  and and_31 (and_31_out, Clock, Writw_Enable, decoder_1_out30);
  and and_32 (and_32_out, Clock, Writw_Enable, decoder_1_out31);
  Register #(.width(32), .Select("low")) register_1 (.D(Din), .Q(register_1_q), .clk(and_1_out));  // open: en, clr
  Register #(.width(32), .Select("low")) register_2 (.D(Din), .Q(register_2_q), .clk(and_2_out));  // open: en, clr
  Register #(.width(32), .Select("low")) register_3 (.D(Din), .Q(register_3_q), .clk(and_3_out));  // open: en, clr
  Register #(.width(32), .Select("low")) register_4 (.D(Din), .Q(register_4_q), .clk(and_4_out));  // open: en, clr
  Register #(.width(32), .Select("low")) register_5 (.D(Din), .Q(register_5_q), .clk(and_5_out));  // open: en, clr
  Register #(.width(32), .Select("low")) register_6 (.D(Din), .Q(register_6_q), .clk(and_6_out));  // open: en, clr
  Register #(.width(32), .Select("low")) register_7 (.D(Din), .Q(register_7_q), .clk(and_7_out));  // open: en, clr
  Register #(.width(32), .Select("low")) register_8 (.D(Din), .Q(register_8_q), .clk(and_8_out));  // open: en, clr
  Register #(.width(32), .Select("low")) register_9 (.D(Din), .Q(register_9_q), .clk(and_9_out));  // open: en, clr
  Register #(.width(32), .Select("low")) register_10 (.D(Din), .Q(register_10_q), .clk(and_10_out));  // open: en, clr
  Register #(.width(32), .Select("low")) register_11 (.D(Din), .Q(register_11_q), .clk(and_11_out));  // open: en, clr
  Register #(.width(32), .Select("low")) register_12 (.D(Din), .Q(register_12_q), .clk(and_12_out));  // open: en, clr
  Register #(.width(32), .Select("low")) register_13 (.D(Din), .Q(register_13_q), .clk(and_13_out));  // open: en, clr
  Register #(.width(32), .Select("low")) register_14 (.D(Din), .Q(register_14_q), .clk(and_14_out));  // open: en, clr
  Register #(.width(32), .Select("low")) register_15 (.D(Din), .Q(register_15_q), .clk(and_15_out));  // open: en, clr
  Register #(.width(32), .Select("low")) register_16 (.D(Din), .Q(register_16_q), .clk(and_16_out));  // open: en, clr
  Register #(.width(32), .Select("low")) register_17 (.D(Din), .Q(register_17_q), .clk(and_17_out));  // open: en, clr
  Register #(.width(32), .Select("low")) register_18 (.D(Din), .Q(register_18_q), .clk(and_18_out));  // open: en, clr
  Register #(.width(32), .Select("low")) register_19 (.D(Din), .Q(register_19_q), .clk(and_19_out));  // open: en, clr
  Register #(.width(32), .Select("low")) register_20 (.D(Din), .Q(register_20_q), .clk(and_20_out));  // open: en, clr
  Register #(.width(32), .Select("low")) register_21 (.D(Din), .Q(register_21_q), .clk(and_21_out));  // open: en, clr
  Register #(.width(32), .Select("low")) register_22 (.D(Din), .Q(register_22_q), .clk(and_22_out));  // open: en, clr
  Register #(.width(32), .Select("low")) register_23 (.D(Din), .Q(register_23_q), .clk(and_23_out));  // open: en, clr
  Register #(.width(32), .Select("low")) register_24 (.D(Din), .Q(register_24_q));  // open: en, clk, clr
  Register #(.width(32), .Select("low")) register_25 (.D(Din), .Q(register_25_q), .clk(and_25_out));  // open: en, clr
  Register #(.width(32), .Select("low")) register_26 (.D(Din), .Q(register_26_q), .clk(and_26_out));  // open: en, clr
  Register #(.width(32), .Select("low")) register_27 (.D(Din), .Q(register_27_q), .clk(and_27_out));  // open: en, clr
  Register #(.width(32), .Select("low")) register_28 (.D(Din), .Q(register_28_q), .clk(and_28_out));  // open: en, clr
  Register #(.width(32), .Select("low")) register_29 (.D(Din), .Q(register_29_q), .clk(and_29_out));  // open: en, clr
  Register #(.width(32), .Select("low")) register_30 (.D(Din), .Q(register_30_q), .clk(and_30_out));  // open: en, clr
  Register #(.width(32), .Select("low")) register_31 (.D(Din), .Q(register_31_q), .clk(and_31_out));  // open: en, clr
  Register #(.width(32), .Select("low")) register_32 (.D(Din), .Q(register_32_q), .clk(and_32_out));  // open: en, clr
  Multiplexer #(.select(5), .width(32), .enable("false")) multiplexer_1 (
    .in0(register_1_q), .in1(register_2_q), .in2(register_3_q), .in3(register_4_q), .in4(register_5_q),
    .in5(register_6_q), .in6(register_7_q), .in7(register_8_q), .in8(register_9_q), .in9(register_10_q),
    .in10(register_11_q), .in11(register_12_q), .in12(register_13_q), .in13(register_14_q),
    .in14(register_15_q), .in15(register_16_q), .in16(register_17_q), .in17(register_18_q),
    .in18(register_19_q), .in19(register_20_q), .in20(register_21_q), .in21(register_22_q),
    .in22(register_23_q), .in23(register_24_q), .in24(register_25_q), .in25(register_26_q),
    .in26(register_27_q), .in27(register_28_q), .in28(register_29_q), .in29(register_30_q),
    .in30(register_31_q), .in31(register_32_q), .out(Reg1Out), .sel(R1_num));
  Multiplexer #(.select(5), .width(32), .enable("false")) multiplexer_2 (
    .in0(register_1_q), .in1(register_2_q), .in2(register_3_q), .in3(register_4_q), .in4(register_5_q),
    .in5(register_6_q), .in6(register_7_q), .in7(register_8_q), .in8(register_9_q), .in9(register_10_q),
    .in10(register_11_q), .in11(register_12_q), .in12(register_13_q), .in13(register_14_q),
    .in14(register_15_q), .in15(register_16_q), .in16(register_17_q), .in17(register_18_q),
    .in18(register_19_q), .in19(register_20_q), .in20(register_21_q), .in21(register_22_q),
    .in22(register_23_q), .in23(register_24_q), .in24(register_25_q), .in25(register_26_q),
    .in26(register_27_q), .in27(register_28_q), .in28(register_29_q), .in29(register_30_q),
    .in30(register_31_q), .in31(register_32_q), .out(Reg2Out), .sel(R2_num));

  // Other names for the same wires on the sheet: CLK = Clock; RA[4:0] = R1_num; RB[4:0] = R2_num; RDA[31:0] = Reg1Out;
  //   RDB[31:0] = Reg2Out; RW[4:0] = Wtite_Reg_num; WE = Writw_Enable

  // Notes on the sheet:
  //   寄存器堆Regfile实现
  //   输入引脚
  //   输出引脚
endmodule

module \寄存器堆Regfile读写测试电路  (
  input  [4:0] \RB_选择读哪个寄存器 ,
  input  [4:0] \RA_选择读哪个寄存器 ,
  input  [4:0] \Write_Reg_选择写哪个寄存器 ,
  input  [31:0] \Din_数据 ,
  input  \WE_使能 ,
  output [31:0] \Reg1Out_读寄存器1 ,
  output [31:0] \Reg2Out_读寄存器2 
);

  wire \CLK_时钟_out ;

  Clock \CLK_时钟  (.out(\CLK_时钟_out ));
  \寄存器堆Regfile实现  \u_寄存器堆regfile实现_1  (
    .R1_num(\RA_选择读哪个寄存器 ), .R2_num(\RB_选择读哪个寄存器 ), .Wtite_Reg_num(\Write_Reg_选择写哪个寄存器 ),
    .Writw_Enable(\WE_使能 ), .Clock(\CLK_时钟_out ), .Din(\Din_数据 ), .Reg1Out(\Reg1Out_读寄存器1 ),
    .Reg2Out(\Reg2Out_读寄存器2 ));

  // Notes on the sheet:
  //   寄存器堆Regfile读写测试电路
endmodule
