// Logisim project chapter-2.circ as structural Verilog: 9 circuits, main circuit CLA
module CLA (
  input  [3:0] A,
  input  [3:0] B,
  input  C0,
  output C4,
  output Gg,
  output C3,
  output [3:0] S,
  output Pg
);

  wire and_1_out, and_2_out, and_3_out, and_5_out, and_6_out, and_7_out, and_8_out, and_10_out, and_11_out,
       nand_1_out, nand_2_out, nand_3_out, nand_4_out, nor_1_out, nor_2_out, nor_3_out, nor_4_out, not_1_out,
       not_2_out, not_3_out, not_4_out, not_5_out, not_6_out, not_7_out, or_2_out, or_3_out, or_4_out,
       or_5_out, or_6_out, or_7_out, or_8_out, or_9_out, or_10_out, or_11_out;

  nand nand_1 (nand_1_out, B[3], A[3]);
  nor nor_1 (nor_1_out, B[3], A[3]);
  nand nand_2 (nand_2_out, B[2], A[2]);
  nor nor_2 (nor_2_out, B[2], A[2]);
  nand nand_3 (nand_3_out, B[1], A[1]);
  nor nor_3 (nor_3_out, B[1], A[1]);
  nand nand_4 (nand_4_out, B[0], A[0]);
  nor nor_4 (nor_4_out, B[0], A[0]);
  not not_1 (not_1_out, C0);
  not not_2 (not_2_out, nand_1_out);
  and and_1 (and_1_out, ~nor_1_out, ~nand_2_out);  // AND_Gate
  and and_2 (and_2_out, ~nor_1_out, ~nand_3_out, ~nor_2_out);  // AND_Gate
  and and_3 (and_3_out, ~nor_1_out, ~nor_2_out, ~nor_3_out, ~nand_4_out);  // AND_Gate
  or or_1 (Gg, not_2_out, and_1_out, and_2_out, and_3_out);
  and and_4 (Pg, ~nor_1_out, ~nor_2_out, ~nor_3_out, ~nor_4_out);  // AND_Gate
  not not_3 (not_3_out, nor_1_out);
  or or_2 (or_2_out, ~nor_2_out, ~nand_1_out);  // OR_Gate
  or or_3 (or_3_out, ~nor_3_out, ~nand_1_out, ~nand_2_out);  // OR_Gate
  or or_4 (or_4_out, ~nor_4_out, ~nand_1_out, ~nand_2_out, ~nand_3_out);  // OR_Gate
  or or_5 (or_5_out, ~nand_1_out, ~nand_2_out, ~nand_3_out, ~nand_4_out, ~not_1_out);  // OR_Gate
  and and_5 (and_5_out, nand_1_out, ~nor_1_out);  // AND_Gate
  not not_4 (not_4_out, nor_2_out);
  or or_6 (or_6_out, ~nor_3_out, ~nand_2_out);  // OR_Gate
  or or_7 (or_7_out, ~nor_4_out, ~nand_2_out, ~nand_3_out);  // OR_Gate
  or or_8 (or_8_out, ~nand_2_out, ~nand_3_out, ~nand_4_out, ~not_1_out);  // OR_Gate
  and and_6 (and_6_out, nand_2_out, ~nor_2_out);  // AND_Gate
  not not_5 (not_5_out, nor_3_out);
  or or_9 (or_9_out, ~nor_4_out, ~nand_3_out);  // OR_Gate
  or or_10 (or_10_out, ~nand_3_out, ~nand_4_out, ~not_1_out);  // OR_Gate
  and and_7 (and_7_out, nand_3_out, ~nor_3_out);  // AND_Gate
  not not_6 (not_6_out, nor_4_out);
  or or_11 (or_11_out, ~nand_4_out, ~not_1_out);  // OR_Gate
  and and_8 (and_8_out, nand_4_out, ~nor_4_out);  // AND_Gate
  not not_7 (not_7_out, not_1_out);
  and and_9 (C3, not_4_out, or_6_out, or_7_out, or_8_out);
  and and_10 (and_10_out, not_5_out, or_9_out, or_10_out);
  and and_11 (and_11_out, not_6_out, or_11_out);
  and and_12 (C4, not_3_out, or_2_out, or_3_out, or_4_out, or_5_out);
  xor xor_1 (S[3], and_5_out, C3);
  xor xor_2 (S[2], and_6_out, and_10_out);
  xor xor_3 (S[1], and_7_out, and_11_out);
  xor xor_4 (S[0], and_8_out, not_7_out);

  // Notes on the sheet:
  //   CLA
endmodule

module CLU (
  input  G3,
  input  P3,
  input  G2,
  input  P2,
  input  G1,
  input  P1,
  input  G0,
  input  P0,
  input  C0,
  output Gs0,
  output C4,
  output C3,
  output C2,
  output C1,
  output Ps0
);

  wire and_2_out, and_3_out, and_4_out, and_5_out, and_6_out, and_7_out, and_8_out, and_9_out, and_10_out,
       and_11_out;

  and and_1 (Ps0, P0, P1, P2, P3);
  and and_2 (and_2_out, P3, G2);
  and and_3 (and_3_out, P3, P2, G1);
  and and_4 (and_4_out, P3, P2, P1, G0);
  and and_5 (and_5_out, P3, P2, P1, P0, C0);
  and and_6 (and_6_out, P2, G1);
  and and_7 (and_7_out, P2, P1, G0);
  and and_8 (and_8_out, P2, P1, P0, C0);
  and and_9 (and_9_out, P1, G0);
  and and_10 (and_10_out, P1, P0, C0);
  and and_11 (and_11_out, P0, C0);
  or or_1 (Gs0, G3, and_2_out, and_3_out, and_4_out);
  or or_2 (C3, G2, and_6_out, and_7_out, and_8_out);
  or or_3 (C2, G1, and_9_out, and_10_out);
  or or_4 (C1, G0, and_11_out);
  or or_5 (C4, Gs0, and_5_out);

  // Notes on the sheet:
  //   CLU
endmodule

module \_16位先行进位加法器  (
  input  [15:0] A,
  input  [15:0] B,
  input  C0,
  output C16,
  output C15,
  output Gs0,
  output Ps0,
  output [15:0] S
);

  wire cla_1_gg, cla_1_pg, cla_2_gg, cla_2_pg, cla_3_gg, cla_3_pg, cla_4_gg, cla_4_pg, clu_1_c1, clu_1_c2,
       clu_1_c3;

  CLA cla_1 (.A(A[15:12]), .B(B[15:12]), .C0(clu_1_c3), .C4(C16), .Gg(cla_1_gg), .C3(C15), .S(S[15:12]), .Pg(cla_1_pg));
  CLA cla_2 (.A(A[11:8]), .B(B[11:8]), .C0(clu_1_c2), .Gg(cla_2_gg), .S(S[11:8]), .Pg(cla_2_pg));  // open: C4, C3
  CLA cla_3 (.A(A[7:4]), .B(B[7:4]), .C0(clu_1_c1), .Gg(cla_3_gg), .S(S[7:4]), .Pg(cla_3_pg));  // open: C4, C3
  CLA cla_4 (.A(A[3:0]), .B(B[3:0]), .C0(C0), .Gg(cla_4_gg), .S(S[3:0]), .Pg(cla_4_pg));  // open: C4, C3
  CLU clu_1 (
    .G3(cla_1_gg), .P3(cla_1_pg), .G2(cla_2_gg), .P2(cla_2_pg), .G1(cla_3_gg), .P1(cla_3_pg), .G0(cla_4_gg),
    .P0(cla_4_pg), .C0(C0), .Gs0(Gs0), .C3(clu_1_c3), .C2(clu_1_c2), .C1(clu_1_c1), .Ps0(Ps0));  // open: C4

  // Notes on the sheet:
  //   16位先行进位加法器
endmodule

module \_32位先行进位加法器  (
  input  Cin,
  input  [31:0] A,
  input  [31:0] B,
  output ZF,
  output [31:0] F,
  output OF,
  output COUT,
  output CF,
  output SF
);

  wire _0_15_c16, _16_31_c15;

  \_16位先行进位加法器  _0_15 (.A(A[15:0]), .B(B[15:0]), .C0(Cin), .C16(_0_15_c16), .S(F[15:0]));  // open: C15, Gs0, Ps0
  \_16位先行进位加法器  _16_31 (
    .A(A[31:16]), .B(B[31:16]), .C0(_0_15_c16), .C16(COUT), .C15(_16_31_c15), .S(F[31:16]));  // open: Gs0, Ps0
  nor nor_1 (ZF, F[31], F[30], F[29], F[28], F[27], F[26], F[25], F[24], F[23], F[22], F[21], F[20], F[19], F[18], F[17], F[16], F[15], F[14], F[13], F[12], F[11], F[10], F[9], F[8], F[7], F[6], F[5], F[4], F[3], F[2], F[1], F[0]);
  xor xor_1 (OF, COUT, _16_31_c15);
  xor xor_2 (CF, COUT, Cin);

  assign SF = F[31];

  // Notes on the sheet:
  //   32位先行进位加法器
endmodule

module ALUctr (
  input  [3:0] ALUctr,
  output [1:0] OPctr,
  output SIGctr,
  output SUBctr
);

  wire and_1_out, and_2_out, and_3_out, and_4_out, and_5_out;

  and and_1 (and_1_out, ~ALUctr[0], ~ALUctr[3], ALUctr[2], ALUctr[1]);  // AND_Gate
  and and_2 (and_2_out, ALUctr[1], ~ALUctr[2], ~ALUctr[3]);  // AND_Gate
  and and_3 (and_3_out, ALUctr[0], ALUctr[1], ALUctr[2], ALUctr[3]);
  and and_4 (and_4_out, ALUctr[1], ~ALUctr[2], ~ALUctr[3]);  // AND_Gate
  and and_5 (and_5_out, ALUctr[1], ~ALUctr[2], ~ALUctr[3]);  // AND_Gate
  or or_1 (OPctr[0], and_1_out, and_2_out);
  or or_2 (OPctr[1], and_3_out, and_4_out);
  not not_1 (SIGctr, ALUctr[0]);
  or or_3 (SUBctr, and_5_out, ALUctr[3]);

  // Notes on the sheet:
  //   ALUctr
endmodule

module ALU (
  input  [31:0] A,
  input  [31:0] B,
  input  [3:0] ALUctr,
  output [31:0] out_4,
  output out_5,
  output out_6,
  output out_7,
  output out_8
);

  wire aluctr_1_sigctr, aluctr_1_subctr, multiplexer_2_out, xor_2_out;
  wire [1:0] aluctr_1_opctr;
  wire [31:0] bit_extender_1_out, bit_extender_2_out, \n32位先行进位加法器_1_f , or_1_out, xor_1_out;

  assign xor_1_out = B ^ bit_extender_1_out;  // XOR_Gate xor_1, 32 bits wide
  assign bit_extender_1_out = {{31{aluctr_1_subctr}}, aluctr_1_subctr};  // Bit_Extender bit_extender_1
  assign or_1_out = A | B;  // OR_Gate or_1, 32 bits wide
  // Probe on A
  \_32位先行进位加法器  \u_32位先行进位加法器_1  (
    .Cin(aluctr_1_subctr), .A(A), .B(xor_1_out), .ZF(out_8), .F(\n32位先行进位加法器_1_f ), .OF(out_5), .CF(out_7),
    .SF(out_6));  // open: COUT
  xor xor_2 (xor_2_out, out_5, out_6);
  Multiplexer #(.select(2), .width(32), .enable("false")) multiplexer_1 (
    .in0(\n32位先行进位加法器_1_f ), .in1(or_1_out), .in2(B), .in3(bit_extender_2_out), .out(out_4),
    .sel(aluctr_1_opctr));
  ALUctr aluctr_1 (.ALUctr(ALUctr), .OPctr(aluctr_1_opctr), .SUBctr(aluctr_1_subctr), .SIGctr(aluctr_1_sigctr));
  // Probe on B
  // Probe on out_4
  Multiplexer #(.enable("false")) multiplexer_2 (
    .in0(out_7), .in1(xor_2_out), .out(multiplexer_2_out), .sel(aluctr_1_sigctr));
  assign bit_extender_2_out = {{31{1'b0}}, multiplexer_2_out};  // Bit_Extender bit_extender_2
  // Probe on aluctr_1_subctr
  // Probe on aluctr_1_opctr
  // Probe on aluctr_1_sigctr

  // Other names for the same wires on the sheet: CF = out_7; OF = out_5; Result[31:0] = out_4; SF = out_6;
  //   Zero = out_8

  // Notes on the sheet:
  //   ALU
  //   ALU输入输出接口
endmodule

module \RAM读写实验  (
  input  [11:0] \地址数据 ,
  input  [31:0] \输入数据 ,
  input  \输入使能 ,
  input  \片选 ,
  input  \输出使能 ,
  output [31:0] \输出数据 
);

  wire \时钟_out , \清零按钮_out ;

  Clock \u_时钟  (.out(\时钟_out ));
  Button \u_清零按钮  (.out(\清零按钮_out ));
  RAM #(.addrWidth(12), .dataWidth(32), .bus("separate"), .simpleMode("false"), .Select("low")) RAM (
    .addr(\地址数据 ), .din(\输入数据 ), .data(\输出数据 ), .str(\输入使能 ), .sel(\片选 ), .clk(\时钟_out ), .ld(\输出使能 ),
    .clr(\清零按钮_out ));

  // Notes on the sheet:
  //   32116160100
  //   RAM读写实验
endmodule

module \RAM_文本终端  (
  input  [11:0] \地址数据 ,
  input  [7:0] \输入数据 ,
  input  \输入使能 ,
  input  \片选 ,
  input  \输出使能 ,
  input  \终端写入使能 
);

  wire \时钟_out , \清零按钮_out , \终端清屏按钮_out ;
  wire [7:0] RAM_data;

  Clock \u_时钟  (.out(\时钟_out ));
  Button \u_清零按钮  (.out(\清零按钮_out ));
  Button \u_终端清屏按钮  (.out(\终端清屏按钮_out ));
  RAM #(.addrWidth(12), .bus("separate"), .simpleMode("false"), .Select("low")) RAM (
    .addr(\地址数据 ), .din(\输入数据 ), .data(RAM_data), .str(\输入使能 ), .sel(\片选 ), .clk(\时钟_out ), .ld(\输出使能 ),
    .clr(\清零按钮_out ));
  TTY tty_1 (.data(RAM_data[6:0]), .clk(\时钟_out ), .we(\终端写入使能 ), .clr(\终端清屏按钮_out ));

  // Notes on the sheet:
  //   Feng Wei ming
  //   RAM-文本终端
endmodule

module \RAM_读取文件  (
);

  RAM #(.addrWidth(11), .dataWidth(32), .bus("separate"), .simpleMode("false"), .Select("low")) RAM ();  // open: addr, din, data, str, sel, clk, ld, clr

  // Notes on the sheet:
  //   RAM-读取文件
endmodule
