// Logisim project chapter-4.circ as structural Verilog: 5 circuits, main circuit 主电路
module \立即数扩展器  (
  input  [31:0] in_1,
  input  [2:0] in_2,
  output [31:0] out_3
);

  wire [11:0] bit_extender_4_out;
  wire [19:0] bit_extender_1_out, bit_extender_2_out, bit_extender_3_out;

  assign bit_extender_1_out = {{19{in_1[31]}}, in_1[31]};  // Bit_Extender bit_extender_1
  assign bit_extender_2_out = {{19{in_1[31]}}, in_1[31]};  // Bit_Extender bit_extender_2
  assign bit_extender_3_out = {{19{in_1[31]}}, in_1[31]};  // Bit_Extender bit_extender_3
  assign bit_extender_4_out = {{11{in_1[31]}}, in_1[31]};  // Bit_Extender bit_extender_4
  Multiplexer #(.select(3), .width(32), .enable("false")) multiplexer_1 (
    .in0({bit_extender_1_out, in_1[31:20]}), .in1({in_1[31:12], {12{1'b0}}}),
    .in2({bit_extender_2_out, in_1[31:25], in_1[11:7]}),
    .in3({bit_extender_3_out, in_1[7], in_1[30:25], in_1[11:8], 1'b0}),
    .in4({bit_extender_4_out, in_1[19:12], in_1[20], in_1[30:21], 1'b0}), .in5({32{1'b0}}), .in6({32{1'b0}}),
    .in7({32{1'b0}}), .out(out_3), .sel(in_2));

  // Other names for the same wires on the sheet: Instr[31:0] = in_1; Extop[2:0] = in_2; Imm[31:0] = out_3

  // Notes on the sheet:
  //   I
  //   U
  //   S
  //   B
  //   J
  //   输入
  //   立即数扩展器
  //   输出
endmodule

module \指令解析部件  (
  input  [2:0] ExtOp,
  output [31:0] Imm
);

  wire [2:0] Funct3;
  wire [6:0] Funct7;
  wire [24:0] Instr;

  \立即数扩展器  \u_立即数扩展器_1  (.in_1({Funct7, Instr[24:15], Funct3, Instr[11:0]}), .out_3(Imm), .in_2(ExtOp));
  // Probe on Imm

  // Other names for the same wires on the sheet: OpCode[6:0] = Instr[6:0]; Rd[4:0] = Instr[11:7];
  //   Instr (some bits) = {Funct7, Funct3}; Rs1[4:0] = Instr[19:15]; Rs2[4:0] = Instr[24:20]

  // Notes on the sheet:
  //   指令解析部件
endmodule

module \取指令部件  (
  input  \片选 ,
  input  \输出使能 
);

  wire and_1_out, Branch, Clk, Jump, or_1_out, RESET, Zero, \时钟_out , \清零按钮_out ;
  wire [31:0] adder_1_out, Imm, Instr, multiplexer_1_out, PC_q;

  Register #(.width(32), .Select("low")) PC (.D(adder_1_out), .Q(PC_q), .clk(Clk), .clr(RESET));  // open: en
  and and_1 (and_1_out, Zero, Branch);
  Multiplexer #(.width(32), .enable("false")) multiplexer_1 (
    .in0(32'h4), .in1(Imm), .out(multiplexer_1_out), .sel(or_1_out));
  or or_1 (or_1_out, Jump, and_1_out);
  Adder #(.width(32)) adder_1 (.a(PC_q), .b(multiplexer_1_out), .out(adder_1_out));  // open: cin, cout
  // Probe on multiplexer_1_out
  Clock \u_时钟  (.out(\时钟_out ));
  Button \u_清零按钮  (.out(\清零按钮_out ));
  RAM #(.addrWidth(12), .dataWidth(32), .bus("asynch"), .simpleMode("false"), .Select("low")) ram_1 (
    .addr(PC_q[13:2]), .data(Instr), .sel(\片选 ), .clk(\时钟_out ), .ld(\输出使能 ), .clr(\清零按钮_out ));

  // Notes on the sheet:
  //   取指令部件
endmodule

module \指令控制器  (
  input  [2:0] funct3,
  input  [6:0] opcode,
  output RegWr,
  output [3:0] ALUCtr,
  output MemtoReg,
  output MemWr,
  output [1:0] ALUBSrc,
  output Branch,
  output [2:0] ExtOp,
  output Jump,
  output ALUASrc
);

  wire and_1_out, and_2_out, and_3_out, I_out, lui_out, or_1_out, R_out;

  and R (R_out, opcode[0], opcode[1], ~opcode[2], ~opcode[3], opcode[4], opcode[5], ~opcode[6]);  // AND_Gate
  and I (I_out, opcode[0], opcode[1], ~opcode[2], ~opcode[3], opcode[4], ~opcode[5], ~opcode[6]);  // AND_Gate
  and lui (lui_out, opcode[0], opcode[1], opcode[2], ~opcode[3], opcode[4], opcode[5], ~opcode[6]);  // AND_Gate
  and load (MemtoReg, opcode[0], opcode[1], ~opcode[2], ~opcode[3], ~opcode[4], ~opcode[5], ~opcode[6]);  // AND_Gate
  and store (MemWr, opcode[0], opcode[1], ~opcode[2], ~opcode[3], ~opcode[4], opcode[5], ~opcode[6]);  // AND_Gate
  and b (Branch, opcode[0], opcode[1], ~opcode[2], ~opcode[3], ~opcode[4], opcode[5], opcode[6]);  // AND_Gate
  and j (ALUASrc, opcode[0], opcode[1], opcode[2], opcode[3], ~opcode[4], opcode[5], opcode[6]);  // AND_Gate
  or or_1 (or_1_out, R_out, I_out);
  or or_2 (RegWr, R_out, I_out, lui_out, MemtoReg, ALUASrc);
  and and_1 (and_1_out, or_1_out, funct3[0]);
  and and_2 (and_2_out, or_1_out, funct3[1]);
  and and_3 (and_3_out, or_1_out, funct3[2]);
  or or_3 (ALUCtr[3], lui_out, Branch);
  or or_4 (ALUBSrc[1], MemWr, MemtoReg, lui_out, I_out);
  or or_5 (ExtOp[1], MemWr, Branch);
  or or_6 (ExtOp[0], Branch, lui_out);
  or or_7 (ALUCtr[0], and_1_out, lui_out);
  or or_8 (ALUCtr[1], and_2_out, lui_out);
  or or_9 (ALUCtr[2], and_3_out, lui_out);

  assign ALUBSrc[0] = ALUASrc;
  assign ExtOp[2] = ALUASrc;
  assign Jump = ALUASrc;

  // Notes on the sheet:
  //   指令控制器
endmodule

module \主电路  (
  input  \片选 ,
  input  [31:0] Imm,
  input  Branch,
  input  Jump,
  input  Zero,
  output [31:0] Instr,
  output [6:0] opcode,
  output [4:0] rs1,
  output [2:0] funct3,
  output [4:0] rs2,
  output [4:0] rd,
  output [6:0] funct7,
  output [2:0] extop
);

  wire and_1_out, Clk, or_1_out, RESET;
  wire [31:0] adder_1_out, multiplexer_1_out, PC_q;

  \立即数扩展器  \u_立即数扩展器_1  (.in_1({funct7, Instr[24:15], funct3, Instr[11:0]}), .out_3(Imm), .in_2(extop));
  // Probe on Imm
  \指令控制器  \u_指令控制器_1  (
    .funct3(funct3), .opcode(Instr[6:0]), .ExtOp(extop));  // open: RegWr, ALUCtr, MemtoReg, MemWr, ALUBSrc, Branch, Jump, ALUASrc
  Clock u_clk (.out(Clk));
  Button u_RESET (.out(RESET));
  Register #(.width(32), .Select("low")) PC (.D(adder_1_out), .Q(PC_q), .clk(Clk), .clr(RESET));  // open: en
  and and_1 (and_1_out, Zero, Branch);
  Multiplexer #(.width(32), .enable("false")) multiplexer_1 (
    .in0(32'h4), .in1(Imm), .out(multiplexer_1_out), .sel(or_1_out));
  or or_1 (or_1_out, Jump, and_1_out);
  Adder #(.width(32)) adder_1 (.a(PC_q), .b(multiplexer_1_out), .out(adder_1_out));  // open: cin, cout
  // Probe on multiplexer_1_out
  ROM #(.addrWidth(12), .dataWidth(32), .Select("low")) rom_1 (
    .addr(PC_q[13:2]), .data({funct7, Instr[24:15], funct3, Instr[11:0]}), .sel(\片选 ));

  assign {Instr[31:25], Instr[14:12]} = {funct7, funct3};
  assign opcode = Instr[6:0];
  assign rd = Instr[11:7];
  assign rs1 = Instr[19:15];
  assign rs2 = Instr[24:20];

  // Notes on the sheet:
  //   取指令部件
  //   指令控制
  //   输入信号
  //   指令解析部件
  //   输出信号
  //   contents of rom_1 (hex, n*v repeats v):
  //   12*0 12b7 fff28293 5be1863 288000ef 112623
endmodule
